# Fritzing sketch Adalogger (saved by Fritzing 0.8.7b)
breadboards: 1

parts:
  Bauteil1 = Adafruit Feather M0 Adalogger [part_number="Adafruit #2796"]
  Bauteil2 = u-blox NEO-6M GPS Breakout
  o1 = 1.3 Zoll OLED I2C 128x64 SSD1306 [package=THT]
  M1 = BME280
  S1 = SWITCH_SPDT [package=kps-1290]

nets:
  GND: Bauteil1.GND, Bauteil2.GND, o1.GND, M1.GND, S1.P
  N1: Bauteil1.D1, Bauteil2.RXD
  N2: Bauteil1.D0, Bauteil2.TXD
  +3V3: Bauteil1.+3V3, Bauteil2.VCC, o1.VDD, M1.VIN
  N3: Bauteil1.EN, S1.O
  N4: Bauteil1.SCL, o1.SCL, M1.SCL
  N5: Bauteil1.SDA, o1.SDA, M1.SDA

custom parts:
  Adafruit Feather M0 Adalogger: This is the Adafruit Feather M0 Adalogger - our take on an 'all-in-one' Cortex M0 datalogger (or data-reader) with built in USB and battery charging. Its an Adafruit Feather M0 with a microSD holder ready to rock! We have other boards in the Feather family, check'em out here At the Feather M0's heart is an ATSAMD21G18 ARM Cortex M0 processor, clocked at 48 MHz and at 3.3V logic, the same one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
  BME280: Temperature Humidity Barometric presure Sensor
