# Fritzing sketch AdaloggerV2mpu6050 (saved by Fritzing 0.8.7b)
breadboards: 1

parts:
  Bauteil2 = Adafruit Feather M0 Adalogger [part_number="Adafruit #2796"]
  o2 = 1.3 Zoll OLED I2C 128x64 SSD1306 [package=THT]
  S2 = SWITCH_SPDT [package=kps-1290]
  M3 = NEO-6M GPS Module [part_number=GY-GPS6MV2]
  GY1 = MPU-6050 Board GY-521 [form="♀ (female)" package=THT]

nets:
  GND: Bauteil2.GND, o2.GND, S2.O, M3.GND, GY1.pin2
  N1: Bauteil2.D1, M3.Rx
  N2: Bauteil2.D0, M3.Tx
  +3V3: Bauteil2.+3V3, o2.VDD, M3.Vcc, GY1.pin1
  N3: Bauteil2.EN, S2.P
  N4: Bauteil2.SCL, o2.SCL, GY1.pin3
  N5: Bauteil2.SDA, o2.SDA, GY1.pin4

custom parts:
  Adafruit Feather M0 Adalogger: This is the Adafruit Feather M0 Adalogger - our take on an 'all-in-one' Cortex M0 datalogger (or data-reader) with built in USB and battery charging. Its an Adafruit Feather M0 with a microSD holder ready to rock! We have other boards in the Feather family, check'em out here At the Feather M0's heart is an ATSAMD21G18 ARM Cortex M0 processor, clocked at 48 MHz and at 3.3V logic, the same one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
  NEO-6M GPS Module: GY-GPS6MV2 NEO-6M GPS Module Module based on U-blox NEO-6M GPS engine, incorporating regulator for 3.3-5V DC input, MS621FE-compatible rechargeable battery for backup and EEPROM for storing configuration settings. Links: NEO-6 series product information page NEO-6 Datasheet
  MPU-6050 Board GY-521: Acelerometro y Giroscopio MPU-6050 Board GY-521
